# Fritzing sketch counter_fritzing (saved by Fritzing 0.9.1b)
breadboards: 1

parts:
  Eleman1 = Arduino Uno (Rev3)
  R1 = Resistor [tolerance=±5% resistance=220 package=THT]
  S1 = Pushbutton [package="[THT]"]
  U1 = 7-SEGMENT-DISPLAY-1_-RED [package=7-segment-1_pth]
  R2 = Resistor [tolerance=±5% resistance=220 package=THT]  # not connected

nets:
  N1: Eleman1.D8, U1.G
  N2: Eleman1.D12/MISO, Eleman1.5V, S1.Pin_1, S1.Pin_2
  N3: Eleman1.D2, U1.A
  N4: Eleman1.D3_PWM, U1.B
  N5: Eleman1.D4, U1.C
  N6: Eleman1.D5_PWM, U1.D
  N7: Eleman1.D6_PWM, U1.E
  N8: Eleman1.D7, U1.F
  N9: Eleman1.GND, R1.Pin_0
  N10: S1.Pin_3, S1.Pin_4
  N11: U1.G1, U1.G2
