# Fritzing sketch kapi_guvenlik_fritzing (saved by Fritzing 0.9.0b)
breadboards: 1

parts:
  Part1 = Arduino Uno (Rev3)
  J1 = Piezo Speaker
  LED1 = smd LED [color="Red (633nm)" package="1206 [SMD]"]
  LED2 = smd LED [color="Blue (525nm)" package="1206 [SMD]"]
  U1 = LCD-16X2 [package=lcd-16x2_noholes]
  Part2 = RFID USB Reader

nets:
  N1: Part1.A4/SDA, U1.K
  N2: Part1.A5/SCL, U1.A
  N3: Part1.D10_PWM/SS, Part2.GNDT
  N4: Part1.D11_PWM/MOSI, Part2.ANT2
  N5: Part1.D12/MISO, Part2.ANT1
  N6: Part1.D13/SCK, Part2.CP
  N7: Part1.GND, J1.pin1, LED1.cathode, LED2.cathode, U1.DB6, Part2.TX-O
  N8: Part1.D2, J1.pin2
  N9: Part1.D3_PWM, LED1.anode
  N10: Part1.D4, LED2.anode
  N11: Part1.D5_PWM, Part2.GND
  3V3: Part1.3V3, Part2.VCC
  N12: Part1.5V, U1.DB7

notes:
  Soldan Sağa
  SDA
  SCL
  5V - VCC
  GND
  Soldan Sağa
  SDA - SS
  SCK
  MOSI
  MISO
  IRQ -> (boş)
  GND
  RST
  3.3V
