# Fritzing sketch lcd_fritzing (saved by Fritzing 0.9.1b)
breadboards: 1

parts:
  LCD1 = LCD screen
  Eleman2 = Arduino Uno (Rev3)

nets:
  N1: LCD1.VDD, Eleman2.D13/SCK
  N2: LCD1.V0, Eleman2.A4/SDA
  N3: LCD1.RS, Eleman2.A5/SCL
  N4: LCD1.R/W, Eleman2.GND

notes:
  Aşağıdaki modüller I2C Modülü için geçerlidir.
  Soldan Sağa
  Pin 11 > SCL
  Pin 10 > SDA
  Pin 9 > Ground
  3.3 V > VCC
