# Fritzing sketch servo_joystick_fritzing (saved by Fritzing 0.9.0b)
breadboards: 1

parts:
  Part2 = Arduino Mega ADK (Rev3)
  J1 = Basic Servo
  J2 = Basic Servo
  Part3 = Thumb Joystick

nets:
  N1: Part2.A0, Part3.VERT
  N2: Part2.A1, Part3.HORZ
  N3: Part2.D8_PWM, J2.pulse
  VCC: Part2.5V, J1.vcc, J2.vcc, Part3.VCC
  GND: Part2.GND, J1.gnd, J2.gnd, Part3.GND
  N4: Part2.D7_PWM, J1.pulse
